// Digital circuit bcd_4bits.dig as structural Verilog
module bcd_4bits (
  input  A,
  input  B,
  input  C,
  input  D,
  output a_2,
  output b_2,
  output c_2,
  output d_2,
  output e
);

  wire and_1_out, and_2_out, and_3_out, and_4_out, and_5_out, and_6_out, and_7_out, and_8_out, and_9_out,
       and_10_out, and_11_out, and_12_out, and_13_out, and_14_out, not_1_out, not_2_out, not_3_out,
       not_4_out, not_5_out, not_6_out, not_7_out, not_8_out, not_9_out, not_10_out, not_11_out, not_12_out,
       or_1_out, or_2_out, or_4_out, or_5_out, or_6_out, or_7_out, or_9_out, or_10_out, xor_1_out;

  not not_1 (not_1_out, A);
  not not_2 (not_2_out, B);
  xor xor_1 (xor_1_out, C, D);
  not not_3 (not_3_out, C);
  not not_4 (not_4_out, B);
  not not_5 (not_5_out, C);
  not not_6 (not_6_out, D);
  not not_7 (not_7_out, A);
  not not_8 (not_8_out, A);
  and and_1 (and_1_out, B, D);
  not not_9 (not_9_out, B);
  and and_2 (and_2_out, not_9_out, not_10_out);
  not not_10 (not_10_out, C);
  not not_11 (not_11_out, D);
  or or_1 (or_1_out, B, not_3_out);
  or or_2 (or_2_out, A, not_11_out);
  or or_3 (and_2_out, not_2_out, xor_1_out);
  and and_3 (and_3_out, not_4_out, not_5_out);
  and and_4 (and_4_out, not_7_out, not_6_out);
  or or_4 (or_4_out, and_1_out, C);
  or or_5 (or_5_out, or_1_out, D);
  and and_5 (and_5_out, C, not_6_out);
  and and_6 (and_6_out, B, not_5_out);
  and and_7 (and_7_out, and_2_out, or_2_out);
  and and_8 (and_8_out, not_1_out, and_2_out);
  and and_9 (and_9_out, and_3_out, not_6_out);
  and and_10 (and_10_out, not_7_out, and_3_out);
  and and_11 (and_11_out, and_6_out, D);
  and and_12 (and_12_out, and_4_out, C);
  or or_6 (or_6_out, B, C);
  and and_13 (and_13_out, not_8_out, or_4_out);
  and and_14 (and_14_out, not_1_out, or_5_out);
  or or_7 (or_7_out, and_9_out, and_10_out);
  or or_8 (d_2, or_7_out, or_9_out);
  or or_9 (or_9_out, and_5_out, and_11_out);
  or or_10 (or_10_out, and_12_out, or_6_out);
  or or_11 (a_2, and_13_out, and_7_out);
  or or_12 (b_2, and_2_out, and_8_out);
  or or_13 (c_2, and_14_out, and_2_out);
  not not_12 (not_12_out, or_10_out);
  and and_15 (e, not_12_out, not_5_out);
endmodule
